# Fritzing sketch DS18B20-thermister (saved by Fritzing 1.0.3b)
breadboards: 1

parts:
  part = Arduino Uno (Rev3)
  R1 = Resistor [tolerance=±5% power=0.25W resistance=4.7k package=THT]
  T1 = LM35 Temperature Sensor [thermistor_type=NTC part_number=DS18B20 package="TO92 [THT]"]  # not connected

nets:
  N1: part.D4, R1.Pin_0
  N2: part.5V, R1.Pin_1
