# Fritzing sketch teabagger (saved by Fritzing 1.0.3b)
breadboards: 1

parts:
  A1 = Arduino Uno (Rev3)
  Stepper_motor_controller = Pololu A4988 [package=SO16]
  M1 = Stepper Motor - Bipolar
  C1 = Electrolytic Capacitor [capacitance=0.1mF voltage=50V package="100 mil [THT, electrolytic]"]
  V5 = DC Power [voltage=12V]

nets:
  Pin 10: A1.D10_PWM/SS, Stepper_motor_controller.STEP
  Pin 11: A1.D11_PWM/MOSI, Stepper_motor_controller.DIR
  GND: A1.GND, Stepper_motor_controller.GND, C1.-, V5.V-
  5V: A1.5V, Stepper_motor_controller.VDD
  12V: A1.VIN, Stepper_motor_controller.VMOT, C1.+, V5.V+
  N1: Stepper_motor_controller.RESET, Stepper_motor_controller.SLEEP
  N2: Stepper_motor_controller.1B, M1.D
  N3: Stepper_motor_controller.1A, M1.B
  N4: Stepper_motor_controller.2A, M1.C
  N5: Stepper_motor_controller.2B, M1.A

notes:
  Logic voltage
